# Fritzing sketch Car_Sketch (saved by Fritzing 0.9.3b)
breadboards: 1

parts:
  Atmega1 = ATmega328 [package=tqfp]
  IC1 = H-Bridge [package=THT]
  IC2 = H-Bridge [package=THT]
  M1 = DC Motor
  M2 = DC Motor
  M3 = DC Motor
  M4 = DC Motor
  R1 = Resistor [tolerance=±5% resistance=220 package="2512 [SMD]"]
  C1 = Capacitor [package=cap-pth-small2]
  Part1 = FTDI Basic Programmer

nets:
  N1: Atmega1.PD3(INT1), IC1.1_2EN
  GND: Atmega1.GND, IC1.GND3, IC2.GND3, C1.1, Part1.GND
  5V: Atmega1.VCC, Atmega1.AVCC, IC1.VCC2, IC1.VCC1, IC2.VCC2, IC2.VCC1, R1.Pin_0, C1.2, Part1.POWER
  N2: Atmega1.PD5(T1), IC2.1_2EN
  N3: Atmega1.PD6(AIN0), IC1.3_4EN
  N4: Atmega1.PB1(OC1A), IC2.2A
  N5: Atmega1.PB2(SS_OC1B), IC1.3A
  N6: Atmega1.PB3(MOSI_OC2), IC2.3_4EN
  N7: Atmega1.PB4(MISO), IC1.1A
  N8: Atmega1.PB5(SCK), IC1.2A
  N9: Atmega1.PC0(ADC0), IC1.4A
  N10: Atmega1.PC1(ADC1), IC2.4A
  N11: Atmega1.PC2(ADC2), IC2.3A
  N12: Atmega1.PC6(_RESET), R1.Pin_1
  N13: Atmega1.PD0(RXD), Part1.TXO
  N14: Atmega1.PD1(TXD), Part1.RXI
  N15: Atmega1.PD2(INT0), IC2.1A
  N16: IC1.1Y, M2.pin_1
  N17: IC1.2Y, M2.pin_2
  N18: IC1.3Y, M1.pin_2
  N19: IC1.4Y, M1.pin_1
  N20: IC2.1Y, M4.pin_1
  N21: IC2.2Y, M4.pin_2
  N22: IC2.3Y, M3.pin_2
  N23: IC2.4Y, M3.pin_1
